# Fritzing sketch WemosD1_H2O_DS18B20_DeepSleep_LowPower_v1_1 (saved by Fritzing 0.9.2b)
circuit board: 3.92599cm x 2.50138cm
breadboards: 1

parts:
  DS1 = DS18B20 1-Wire Temperature Sensor [part_number=DS18B20]
  R1 = Resistor [tolerance=±5% resistance=4.7k package=THT]
  H2O = AD22100 - Voltage Output Temperature Sensor with Signal Conditioning [part_number=AD22100]
  JP1 = Header 3 [package=screwterminal-3.5mm-3_lock.007s]
  VCC1 = Battery
  WeMos_D1_Mini1 = WeMos D1 Mini

nets:
  GND: DS1.GND, H2O.GND, VCC1.-, WeMos_D1_Mini1.G
  N1: DS1.DQ, R1.Pin_0, WeMos_D1_Mini1.D4
  N2: DS1.VDD, R1.Pin_1, WeMos_D1_Mini1.D3
  N3: H2O.V+, WeMos_D1_Mini1.D1
  N4: H2O.Vo, WeMos_D1_Mini1.A0
  N5: JP1.2, WeMos_D1_Mini1.RST
  N6: JP1.3, WeMos_D1_Mini1.D0
  N7: VCC1.+, WeMos_D1_Mini1.5V

notes:
  MeteoMex
  terra v1.1
  R1
  J1
  -
  +
  A
  B
  D
